// Logisim project Projet.circ as structural Verilog
module main (
);

  A a_1 ();  // open: in_1, Etat, Sous_systeme, CLK, TEMPS_OUT, Etat_OUT, Boutons_OUT
  Heure heure_1 ();  // open: Boutons, Temps, Etat
  Chronometre chronometre_1 ();  // open: Temps, Boutons, Etat, Afficher, Sous_systeme
endmodule

module A (
  input  [1:0] in_1,
  input  [2:0] Etat,
  input  Sous_systeme,
  input  CLK,
  output [22:0] TEMPS_OUT,
  output [2:0] Etat_OUT,
  output [3:0] Boutons_OUT
);

  wire clock_1_out;
  wire [3:0] a_boutons_1_bc1;

  Clock #(.highDuration(51), .lowDuration(51)) clock_1 (.out(clock_1_out));
  A_temps a_temps_1 (.TempsIN(TEMPS_OUT), .CLK(clock_1_out), .TEMPSOUT(TEMPS_OUT));
  A_Boutons a_boutons_1 (
    .Bouton1(in_1[0]), .Bouton2(in_1[1]), .CLK(clock_1_out), .BC1(a_boutons_1_bc1[0]),
    .BL1(a_boutons_1_bc1[1]), .BC2(a_boutons_1_bc1[2]), .BL2(a_boutons_1_bc1[3]));
  A_def_etat a_def_etat_1 (
    .Boutons_IN(a_boutons_1_bc1), .Etat_IN(Etat_OUT), .sous_Etat(Sous_systeme), .CLK(clock_1_out),
    .Etat_OUT(Etat_OUT), .Boutons_OUT(Boutons_OUT));
endmodule

module A_Boutons (
  input  Bouton1,
  input  Bouton2,
  input  CLK,
  output BC1,
  output BL1,
  output BC2,
  output BL2
);

  wire and_1_out, and_2_out, and_3_out, and_4_out, d_ff_1_q, d_ff_2_q, d_ff_3_q, d_ff_4_q, d_ff_5_q,
       d_ff_6_q, d_ff_7_q, d_ff_8_q, d_ff_9_q, d_ff_10_q, d_ff_11_q, d_ff_12_q, d_ff_13_q, d_ff_14_q,
       d_ff_15_q, d_ff_16_q, undriven, undriven_2;

  D_Flip_Flop d_ff_1 (.D(Bouton1), .clk(CLK), .Q(d_ff_1_q));  // open: Qn, preset, reset
  D_Flip_Flop d_ff_2 (.D(Bouton2), .clk(CLK), .Q(d_ff_2_q));  // open: Qn, preset, reset
  D_Flip_Flop d_ff_3 (.D(d_ff_1_q), .clk(CLK), .Q(d_ff_3_q));  // open: Qn, preset, reset
  D_Flip_Flop d_ff_4 (.D(d_ff_2_q), .clk(CLK), .Q(d_ff_4_q));  // open: Qn, preset, reset
  D_Flip_Flop d_ff_5 (.D(d_ff_3_q), .clk(CLK), .Q(d_ff_5_q));  // open: Qn, preset, reset
  D_Flip_Flop d_ff_6 (.D(d_ff_4_q), .clk(CLK), .Q(d_ff_6_q));  // open: Qn, preset, reset
  and and_1 (and_1_out, ~d_ff_1_q, d_ff_3_q);  // AND_Gate
  D_Flip_Flop d_ff_7 (.D(d_ff_5_q), .clk(CLK), .Q(d_ff_7_q));  // open: Qn, preset, reset
  and and_2 (and_2_out, ~d_ff_2_q, d_ff_4_q);  // AND_Gate
  D_Flip_Flop d_ff_8 (.D(d_ff_6_q), .clk(CLK), .Q(d_ff_8_q));  // open: Qn, preset, reset
  D_Flip_Flop d_ff_9 (.D(d_ff_7_q), .clk(CLK), .Q(d_ff_9_q));  // open: Qn, preset, reset
  D_Flip_Flop d_ff_10 (.D(d_ff_8_q), .clk(CLK), .Q(d_ff_10_q));  // open: Qn, preset, reset
  D_Flip_Flop d_ff_11 (.D(d_ff_9_q), .clk(CLK), .Q(d_ff_11_q));  // open: Qn, preset, reset
  D_Flip_Flop d_ff_12 (.D(d_ff_10_q), .clk(CLK), .Q(d_ff_12_q));  // open: Qn, preset, reset
  D_Flip_Flop d_ff_13 (.D(d_ff_11_q), .clk(CLK), .Q(d_ff_13_q));  // open: Qn, preset, reset
  D_Flip_Flop d_ff_14 (.D(d_ff_12_q), .clk(CLK), .Q(d_ff_14_q));  // open: Qn, preset, reset
  D_Flip_Flop d_ff_15 (.D(d_ff_13_q), .clk(CLK), .Q(d_ff_15_q), .reset(undriven));  // open: Qn, preset
  D_Flip_Flop d_ff_16 (.D(d_ff_14_q), .clk(CLK), .Q(d_ff_16_q), .reset(undriven_2));  // open: Qn, preset
  and and_3 (and_3_out, d_ff_5_q, d_ff_7_q, d_ff_9_q, d_ff_11_q, d_ff_13_q, d_ff_15_q);
  and and_4 (and_4_out, d_ff_6_q, d_ff_8_q, d_ff_10_q, d_ff_12_q, d_ff_14_q, d_ff_16_q);
  and and_5 (BC1, ~and_3_out, and_1_out);  // AND_Gate
  and and_6 (BL1, and_3_out, and_1_out);
  and and_7 (BC2, ~and_4_out, and_2_out);  // AND_Gate
  and and_8 (BL2, and_4_out, and_2_out);
endmodule

module A_temps (
  input  [22:0] TempsIN,
  input  CLK,
  output [22:0] TEMPSOUT
);

  wire comparator_1_eq;
  wire [22:0] adder_1_out, register_1_q;

  Adder #(.width(23)) adder_1 (.a(TempsIN), .b(23'h1), .out(adder_1_out));  // open: cin, cout
  Register #(.width(23)) register_1 (.D(adder_1_out), .clk(CLK), .Q(register_1_q));  // open: en, clr
  Comparator #(.width(23), .mode("unsigned")) comparator_1 (
    .a(register_1_q), .b(23'h5c4900), .eq(comparator_1_eq));  // open: gt, lt
  Multiplexer #(.width(23), .enable("false")) multiplexer_1 (
    .in0(register_1_q), .in1({23{1'b0}}), .out(TEMPSOUT), .sel(comparator_1_eq));
endmodule

module A_def_etat (
  input  [3:0] Boutons_IN,
  input  [2:0] Etat_IN,
  input  sous_Etat,
  input  CLK,
  output [2:0] Etat_OUT,
  output [3:0] Boutons_OUT
);

  wire and_2_out, and_3_out, not_1_out, not_2_out, not_3_out, not_4_out, not_5_out, not_6_out, or_1_out;
  wire [1:0] and_4_out;
  wire [2:0] multiplexer_1_out;

  not not_1 (not_1_out, Etat_IN[2]);
  not not_2 (not_2_out, Etat_IN[1]);
  not not_3 (not_3_out, Etat_IN[2]);
  not not_4 (not_4_out, Etat_IN[0]);
  not not_5 (not_5_out, Etat_IN[2]);
  not not_6 (not_6_out, Etat_IN[0]);
  or or_1 (or_1_out, sous_Etat, ~Boutons_IN[0]);  // OR_Gate
  and and_1 (Boutons_OUT[0], sous_Etat, Boutons_IN[0]);
  and and_2 (and_2_out, not_1_out, not_2_out, Etat_IN[0]);
  or or_2 (and_4_out[1], and_2_out, and_3_out);
  and and_3 (and_3_out, not_3_out, Etat_IN[1], not_4_out);
  and and_4 (and_4_out[0], not_5_out, not_6_out);
  Register #(.width(3)) register_1 (.D(multiplexer_1_out), .clk(CLK), .Q(Etat_OUT));  // open: en, clr
  Multiplexer #(.width(3), .enable("false")) multiplexer_1 (
    .in0({1'b0, and_4_out}), .in1(Etat_IN), .out(multiplexer_1_out), .sel(or_1_out));

  assign Boutons_OUT[3:1] = Boutons_IN[3:1];
endmodule

module Heure (
  input  Boutons,
  input  Temps,
  input  Etat
);


  // Notes on the sheet:
  //   CONV:
  //   Affichage
endmodule

module Conv_temps (
  input  [22:0] temps_IN,
  output [2:0] jour_semaine,
  output [4:0] heure,
  output [5:0] minutes,
  output [5:0] secondes,
  output [3:0] diziemes
);

  wire [9:4] divider_4_rem;
  wire [9:6] divider_4_out;
  wire [15:0] divider_3_rem;
  wire [15:6] divider_3_out;
  wire [19:0] divider_2_rem;
  wire [19:5] divider_2_out;
  wire [22:0] divider_1_rem;
  wire [22:3] divider_1_out;

  Divider #(.width(23)) divider_1 (
    .a(temps_IN), .b(23'hd2f00), .out({divider_1_out, jour_semaine}), .rem(divider_1_rem));  // open: upper
  Divider #(.width(20)) divider_2 (
    .a(divider_1_rem[19:0]), .b(20'h8ca0), .out({divider_2_out, heure}), .rem(divider_2_rem));  // open: upper
  Divider #(.width(16)) divider_3 (
    .a(divider_2_rem[15:0]), .b(16'h258), .out({divider_3_out, minutes}), .rem(divider_3_rem));  // open: upper
  Divider #(.width(10)) divider_4 (
    .a(divider_3_rem[9:0]), .b(10'ha), .out({divider_4_out, secondes}), .rem({divider_4_rem, diziemes}));  // open: upper
endmodule

module Chronometre (
  input  [22:0] Temps,
  input  [3:0] Boutons,
  input  [2:0] Etat,
  output [22:0] Afficher,
  output Sous_systeme
);

  wire and_1_out, and_2_out, and_3_out, comparator_1_gt, not_1_out, not_2_out, or_1_out, t_ff_2_q;
  wire [22:0] conteur_tours_1_temps_sortie, Debut_q, FIn_q, multiplexer_1_out, multiplexer_2_out;

  and and_1 (and_1_out, ~Etat[0], Etat[1], ~Etat[2]);  // AND_Gate
  T_Flip_Flop t_ff_1 (.T(and_2_out), .clk(Boutons[2]), .Q(Sous_systeme), .reset(not_1_out));  // open: Qn, preset
  and and_2 (and_2_out, not_2_out, and_1_out);
  not not_1 (not_1_out, and_1_out);
  Register #(.width(23)) Debut (.D(Temps), .clk(Sous_systeme), .Q(Debut_q), .clr(and_3_out));  // open: en
  and and_3 (and_3_out, Boutons[3], and_1_out, ~Sous_systeme);  // AND_Gate
  T_Flip_Flop t_ff_2 (.T(and_1_out), .clk(Boutons[1]), .Q(t_ff_2_q));  // open: Qn, reset, preset
  not not_2 (not_2_out, t_ff_2_q);
  Register #(.width(23), .trigger("falling")) FIn (
    .D(Temps), .clk(Sous_systeme), .Q(FIn_q), .clr(and_3_out));  // open: en
  Comparator #(.width(23), .mode("unsigned")) comparator_1 (
    .a(FIn_q), .b(Debut_q), .gt(comparator_1_gt));  // open: eq, lt
  Multiplexer #(.width(23), .enable("false")) multiplexer_1 (
    .in0(Temps), .in1(FIn_q), .out(multiplexer_1_out), .sel(or_1_out));
  or or_1 (or_1_out, comparator_1_gt, ~Sous_systeme);  // OR_Gate
  Multiplexer #(.width(23), .enable("false")) multiplexer_2 (
    .in0(multiplexer_1_out), .in1(conteur_tours_1_temps_sortie), .out(multiplexer_2_out), .sel(t_ff_2_q));
  Conteur_tours conteur_tours_1 (
    .B1L(Boutons[1]), .B1C(Boutons[0]), .Sous_syst(Sous_systeme), .Lect_tours(t_ff_2_q), .Reset(and_3_out),
    .Temps(Temps), .Debut(Debut_q), .temps_sortie(conteur_tours_1_temps_sortie));
  Subtractor #(.width(23)) subtractor_1 (.a(multiplexer_2_out), .b(Debut_q), .out(Afficher));  // open: bin, bout
endmodule

module Conteur_tours (
  input  B1L,
  input  B1C,
  input  Sous_syst,
  input  Lect_tours,
  input  Reset,
  input  [22:0] Temps,
  input  [22:0] Debut,
  output [22:0] temps_sortie
);

  wire and_1_out, and_2_out, and_3_out, and_4_out, and_5_out, and_6_out, and_7_out, and_8_out,
       comparator_1_lt, comparator_2_lt, comparator_3_lt, comparator_4_lt, comparator_5_lt, comparator_6_lt,
       comparator_7_lt, d_ff_1_q, d_ff_2_q, d_ff_3_q, d_ff_4_q, d_ff_5_q, d_ff_6_q, d_ff_7_q, d_ff_8_q,
       nor_1_out, not_1_out, or_1_out, or_2_out, or_3_out, or_4_out, or_5_out, or_6_out, or_7_out, or_8_out,
       or_9_out, or_10_out;
  wire [22:0] controlled_buffer_1_out, controlled_buffer_2_out, controlled_buffer_3_out,
       controlled_buffer_4_out, controlled_buffer_5_out, controlled_buffer_6_out, controlled_buffer_7_out,
       register_1_q, register_2_q, register_3_q, register_4_q, register_5_q, register_6_q, register_7_q;

  or or_1 (or_1_out, Sous_syst, Lect_tours);
  and and_1 (and_1_out, or_1_out, B1C);
  D_Flip_Flop d_ff_1 (.D(1'b1), .clk(and_1_out), .Q(d_ff_1_q), .reset(or_3_out));  // open: Qn, preset
  D_Flip_Flop d_ff_2 (.D(d_ff_1_q), .clk(and_1_out), .Q(d_ff_2_q), .reset(or_4_out));  // open: Qn, preset
  D_Flip_Flop d_ff_3 (.D(d_ff_2_q), .clk(and_1_out), .Q(d_ff_3_q), .reset(or_5_out));  // open: Qn, preset
  D_Flip_Flop d_ff_4 (.D(d_ff_3_q), .clk(and_1_out), .Q(d_ff_4_q), .reset(or_6_out));  // open: Qn, preset
  D_Flip_Flop d_ff_5 (.D(d_ff_4_q), .clk(and_1_out), .Q(d_ff_5_q), .reset(or_7_out));  // open: Qn, preset
  D_Flip_Flop d_ff_6 (.D(d_ff_5_q), .clk(and_1_out), .Q(d_ff_6_q), .reset(or_8_out));  // open: Qn, preset
  D_Flip_Flop d_ff_7 (.D(d_ff_6_q), .clk(and_1_out), .Q(d_ff_7_q), .reset(or_9_out));  // open: Qn, preset
  D_Flip_Flop d_ff_8 (.D(or_2_out), .clk(and_1_out), .Q(d_ff_8_q), .reset(or_10_out));  // open: Qn, preset
  or or_2 (or_2_out, d_ff_7_q, d_ff_8_q);
  or or_3 (or_3_out, d_ff_2_q, or_4_out);
  or or_4 (or_4_out, d_ff_3_q, or_5_out);
  or or_5 (or_5_out, d_ff_4_q, or_6_out);
  or or_6 (or_6_out, d_ff_5_q, or_7_out);
  or or_7 (or_7_out, d_ff_6_q, or_8_out);
  or or_8 (or_8_out, d_ff_7_q, or_9_out);
  or or_9 (or_9_out, d_ff_8_q, or_10_out);
  or or_10 (or_10_out, Reset, B1L);
  Register #(.width(23)) register_1 (.D(Temps), .en(not_1_out), .clk(d_ff_1_q), .Q(register_1_q), .clr(Reset));
  not not_1 (not_1_out, Lect_tours);
  Register #(.width(23)) register_2 (.D(Temps), .en(not_1_out), .clk(d_ff_2_q), .Q(register_2_q), .clr(Reset));
  Register #(.width(23)) register_3 (.D(Temps), .en(not_1_out), .clk(d_ff_3_q), .Q(register_3_q), .clr(Reset));
  Register #(.width(23)) register_4 (.D(Temps), .en(not_1_out), .clk(d_ff_4_q), .Q(register_4_q), .clr(Reset));
  Register #(.width(23)) register_5 (.D(Temps), .en(not_1_out), .clk(d_ff_5_q), .Q(register_5_q), .clr(Reset));
  Register #(.width(23)) register_6 (.D(Temps), .en(not_1_out), .clk(d_ff_6_q), .Q(register_6_q), .clr(Reset));
  Register #(.width(23)) register_7 (.D(Temps), .en(not_1_out), .clk(d_ff_7_q), .Q(register_7_q), .clr(Reset));
  assign controlled_buffer_1_out = d_ff_1_q ? register_1_q : 23'bz;  // Controlled_Buffer controlled_buffer_1
  assign controlled_buffer_2_out = d_ff_2_q ? register_2_q : 23'bz;  // Controlled_Buffer controlled_buffer_2
  assign controlled_buffer_3_out = d_ff_3_q ? register_3_q : 23'bz;  // Controlled_Buffer controlled_buffer_3
  assign controlled_buffer_4_out = d_ff_4_q ? register_4_q : 23'bz;  // Controlled_Buffer controlled_buffer_4
  assign controlled_buffer_5_out = d_ff_5_q ? register_5_q : 23'bz;  // Controlled_Buffer controlled_buffer_5
  assign controlled_buffer_6_out = d_ff_6_q ? register_6_q : 23'bz;  // Controlled_Buffer controlled_buffer_6
  assign controlled_buffer_7_out = d_ff_7_q ? register_7_q : 23'bz;  // Controlled_Buffer controlled_buffer_7
  assign temps_sortie = nor_1_out ? Debut : 23'bz;  // Controlled_Buffer controlled_buffer_8
  Comparator #(.width(23)) comparator_1 (.a(Debut), .b(register_1_q), .lt(comparator_1_lt));  // open: gt, eq
  assign temps_sortie = comparator_1_lt ? controlled_buffer_1_out : 23'bz;  // Controlled_Buffer controlled_buffer_9
  Comparator #(.width(23)) comparator_2 (.a(Debut), .b(register_2_q), .lt(comparator_2_lt));  // open: gt, eq
  assign temps_sortie = comparator_2_lt ? controlled_buffer_2_out : 23'bz;  // Controlled_Buffer controlled_buffer_10
  Comparator #(.width(23)) comparator_3 (.a(Debut), .b(register_3_q), .lt(comparator_3_lt));  // open: gt, eq
  assign temps_sortie = comparator_3_lt ? controlled_buffer_3_out : 23'bz;  // Controlled_Buffer controlled_buffer_11
  Comparator #(.width(23)) comparator_4 (.a(Debut), .b(register_4_q), .lt(comparator_4_lt));  // open: gt, eq
  assign temps_sortie = comparator_4_lt ? controlled_buffer_4_out : 23'bz;  // Controlled_Buffer controlled_buffer_12
  Comparator #(.width(23)) comparator_5 (.a(Debut), .b(register_5_q), .lt(comparator_5_lt));  // open: gt, eq
  assign temps_sortie = comparator_5_lt ? controlled_buffer_5_out : 23'bz;  // Controlled_Buffer controlled_buffer_13
  Comparator #(.width(23)) comparator_6 (.a(Debut), .b(register_6_q), .lt(comparator_6_lt));  // open: gt, eq
  assign temps_sortie = comparator_6_lt ? controlled_buffer_6_out : 23'bz;  // Controlled_Buffer controlled_buffer_14
  Comparator #(.width(23)) comparator_7 (.a(Debut), .b(register_7_q), .lt(comparator_7_lt));  // open: gt, eq
  assign temps_sortie = comparator_7_lt ? controlled_buffer_7_out : 23'bz;  // Controlled_Buffer controlled_buffer_15
  and and_2 (and_2_out, comparator_1_lt, d_ff_1_q);
  and and_3 (and_3_out, comparator_2_lt, d_ff_2_q);
  and and_4 (and_4_out, comparator_3_lt, d_ff_3_q);
  and and_5 (and_5_out, comparator_4_lt, d_ff_4_q);
  and and_6 (and_6_out, comparator_5_lt, d_ff_5_q);
  and and_7 (and_7_out, comparator_6_lt, d_ff_6_q);
  and and_8 (and_8_out, comparator_7_lt, d_ff_7_q);
  nor nor_1 (nor_1_out, and_2_out, and_3_out, and_4_out, and_5_out, and_6_out, and_7_out, and_8_out);
endmodule

module Alarme (
  input  [22:0] Temps,
  input  [3:0] Boutons,
  input  [2:0] Etat,
  output Sous_systeme,
  output [22:0] out_5,
  output [22:0] out_6,
  output [22:0] out_7
);

  wire and_1_out, and_2_out, and_3_out, and_4_out, and_5_out, and_6_out, and_7_out, d_ff_1_q, d_ff_2_q,
       J1_out, J2_q, J3_q, J4_q, J5_q, J6_q, J7_q, or_1_out, or_2_out, or_3_out, or_4_out, or_5_out,
       set_alarme_1_est_actif, set_alarme_2_est_actif;
  wire [22:0] controlled_buffer_1_out;

  and and_1 (and_1_out, Etat[0], ~Etat[1], ~Etat[2]);  // AND_Gate
  and and_2 (and_2_out, Boutons[2], ~Sous_systeme);  // AND_Gate
  and and_3 (and_3_out, Boutons[2], Sous_systeme);
  T_Flip_Flop t_ff_1 (.T(1'b1), .clk(and_4_out), .Q(Sous_systeme));  // open: Qn, reset, preset
  and and_4 (and_4_out, Boutons[1], and_1_out);
  D_Flip_Flop J2 (.D(1'b1), .clk(and_2_out), .Q(J2_q), .reset(or_1_out));  // open: Qn, preset
  D_Flip_Flop J3 (.D(J2_q), .clk(and_2_out), .Q(J3_q), .reset(or_2_out));  // open: Qn, preset
  D_Flip_Flop J4 (.D(J3_q), .clk(and_2_out), .Q(J4_q), .reset(or_3_out));  // open: Qn, preset
  D_Flip_Flop J5 (.D(J4_q), .clk(and_2_out), .Q(J5_q), .reset(or_4_out));  // open: Qn, preset
  D_Flip_Flop J6 (.D(J5_q), .clk(and_2_out), .Q(J6_q), .reset(J7_q));  // open: Qn, preset
  D_Flip_Flop J7 (.D(J6_q), .clk(and_2_out), .Q(J7_q));  // open: Qn, preset, reset
  and J1 (J1_out, ~or_1_out, ~J2_q);  // AND_Gate
  or or_1 (or_1_out, J3_q, or_2_out);
  or or_2 (or_2_out, J4_q, or_3_out);
  or or_3 (or_3_out, J5_q, or_4_out);
  or or_4 (or_4_out, J6_q, J7_q);
  and and_5 (and_5_out, Boutons[0], Sous_systeme);
  and and_6 (and_6_out, Boutons[3], Sous_systeme);
  D_Flip_Flop d_ff_1 (.D(1'b1), .clk(and_3_out), .Q(d_ff_1_q), .reset(or_5_out));  // open: Qn, preset
  D_Flip_Flop d_ff_2 (.D(d_ff_1_q), .clk(and_3_out), .Q(d_ff_2_q), .reset(and_4_out));  // open: Qn, preset
  or or_5 (or_5_out, d_ff_2_q, and_4_out);
  and and_7 (and_7_out, ~d_ff_1_q, ~d_ff_2_q);  // AND_Gate
  Set_alarme set_alarme_1 (
    .Nbr_a_ajouter(controlled_buffer_1_out), .add(and_5_out), .est_actif(set_alarme_1_est_actif), .E(J1_out),
    .set_actif(and_6_out), .Valeur(out_5));
  Set_alarme set_alarme_2 (
    .Nbr_a_ajouter(controlled_buffer_1_out), .add(and_5_out), .est_actif(set_alarme_2_est_actif), .E(J2_q),
    .set_actif(and_6_out), .Valeur(out_6));
  Set_alarme set_alarme_3 (
    .Nbr_a_ajouter(controlled_buffer_1_out), .add(and_5_out), .E(J3_q), .set_actif(and_6_out), .Valeur(out_7));  // open: est_actif
  Set_alarme set_alarme_4 (
    .Nbr_a_ajouter(controlled_buffer_1_out), .add(and_5_out), .E(J4_q), .set_actif(and_6_out));  // open: est_actif, Valeur
  Set_alarme set_alarme_5 (
    .Nbr_a_ajouter(controlled_buffer_1_out), .add(and_5_out), .E(J5_q), .set_actif(and_6_out));  // open: est_actif, Valeur
  Set_alarme set_alarme_6 (
    .Nbr_a_ajouter(controlled_buffer_1_out), .add(and_5_out), .E(J6_q), .set_actif(and_6_out));  // open: est_actif, Valeur
  Set_alarme set_alarme_7 (
    .Nbr_a_ajouter(controlled_buffer_1_out), .add(and_5_out), .E(J7_q), .set_actif(and_6_out));  // open: est_actif, Valeur
  assign controlled_buffer_1_out = and_7_out ? 23'h8ca0 : 23'bz;  // Controlled_Buffer controlled_buffer_1
  assign controlled_buffer_1_out = d_ff_1_q ? 23'h1770 : 23'bz;  // Controlled_Buffer controlled_buffer_2
  assign controlled_buffer_1_out = d_ff_2_q ? 23'h258 : 23'bz;  // Controlled_Buffer controlled_buffer_3
endmodule

module Set_alarme (
  input  E,
  input  add,
  input  set_actif,
  input  [22:0] Nbr_a_ajouter,
  output [22:0] Valeur,
  output est_actif
);

  wire and_1_out, and_2_out;
  wire [22:0] adder_1_out;

  and and_1 (and_1_out, add, E);
  and and_2 (and_2_out, E, set_actif);
  Register #(.width(23)) register_1 (.D(adder_1_out), .clk(and_1_out), .Q(Valeur));  // open: en, clr
  T_Flip_Flop t_ff_1 (.T(1'b1), .clk(and_2_out), .Q(est_actif));  // open: Qn, reset, preset
  Adder #(.width(23)) adder_1 (.a(Nbr_a_ajouter), .b(Valeur), .out(adder_1_out));  // open: cin, cout
endmodule
