// Logisim project conv_unit_dizaines.circ as structural Verilog: 1 circuit, main circuit main
module main (
  input  [5:0] Entree,
  output [3:0] dizaine,
  output [3:0] unite_dec
);

  wire [5:4] divider_1_out, divider_1_rem;

  Divider #(.width(6)) divider_1 (
    .a(Entree), .b(6'b001010), .out({divider_1_out, dizaine}), .rem({divider_1_rem, unite_dec}));  // open: upper
endmodule
