// Logisim project timer_.circ as structural Verilog: 12 circuits, main circuit main
module main (
  input  [3:0] boutons,
  input  [2:0] etat,
  input  [22:0] temps,
  output [7:0] Seg0,
  output [7:0] Seg1,
  output [7:0] Seg2,
  output [7:0] Seg3,
  output [7:0] Seg4,
  output [7:0] Seg5,
  output sonne
);

  wire actif_q, and_1_out, and_2_out, and_3_out, and_5_out, and_8_out, and_9_out, and_10_out, and_12_out,
       comparator_1_eq, comparator_2_eq, d_ff_1_q, d_ff_2_q, d_ff_3_q, d_ff_4_q, not_1_out, subtractor_1_bout;
  wire [1:0] or_1_out;
  wire [2:0] regle;
  wire [22:0] adder_1_out, adder_2_out, duree_q, fin_q, multiplexer_1_out, multiplexer_2_out,
       multiplexer_3_out, subtractor_1_out, subtractor_2_out, temps_prevu_q;

  Comparator #(.width(3), .mode("unsigned")) comparator_1 (.a(etat), .b(3'b011), .eq(comparator_1_eq));  // open: gt, lt
  D_Flip_Flop d_ff_1 (.D(1'b1), .clk(and_1_out), .Q(d_ff_1_q), .reset(and_3_out));  // open: Qn, preset
  and and_1 (and_1_out, boutons[1], ~actif_q, comparator_1_eq);  // AND_Gate
  and and_2 (and_2_out, boutons[2], ~d_ff_1_q, comparator_1_eq);  // AND_Gate
  and and_3 (and_3_out, d_ff_1_q, boutons[1], comparator_1_eq, ~and_1_out);  // AND_Gate
  T_Flip_Flop actif (.T(comparator_1_eq), .clk(and_2_out), .Q(actif_q));  // open: Qn, reset, preset
  and and_4 (regle[0], d_ff_1_q, ~d_ff_2_q);  // AND_Gate
  D_Flip_Flop d_ff_2 (.D(d_ff_1_q), .clk(boutons[2]), .Q(d_ff_2_q), .reset(d_ff_4_q));  // open: Qn, preset
  Register #(.width(23)) duree (.D(temps_prevu_q), .clk(and_3_out), .Q(duree_q));  // open: en, clr
  and and_5 (and_5_out, boutons[2], actif_q);
  and and_6 (regle[1], d_ff_2_q, ~d_ff_3_q);  // AND_Gate
  D_Flip_Flop d_ff_3 (.D(d_ff_2_q), .clk(boutons[2]), .Q(d_ff_3_q), .reset(d_ff_4_q));  // open: Qn, preset
  Register #(.width(23)) debut (.D(temps), .clk(and_5_out));  // open: en, Q, clr
  and and_7 (regle[2], d_ff_3_q, ~d_ff_4_q);  // AND_Gate
  D_Flip_Flop d_ff_4 (.D(d_ff_3_q), .clk(boutons[2]), .Q(d_ff_4_q), .reset(d_ff_4_q));  // open: Qn, preset
  Adder #(.width(23)) adder_1 (.a(duree_q), .b(temps), .out(adder_1_out));  // open: cin, cout
  Subtractor #(.width(23)) subtractor_1 (
    .a(adder_1_out), .b(23'h5c4900), .out(subtractor_1_out), .bout(subtractor_1_bout));  // open: bin
  Register #(.width(23)) fin (.D(multiplexer_1_out), .clk(and_5_out), .Q(fin_q));  // open: en, clr
  Multiplexer #(.width(23), .enable("false")) multiplexer_1 (
    .in0(subtractor_1_out), .in1(adder_1_out), .out(multiplexer_1_out), .sel(subtractor_1_bout));
  and and_8 (and_8_out, regle[0], boutons[0]);
  and and_9 (and_9_out, regle[1], boutons[0]);
  and and_10 (and_10_out, regle[2], boutons[0]);
  Comparator #(.width(23), .mode("unsigned")) comparator_2 (
    .a(fin_q), .b(temps), .eq(comparator_2_eq));  // open: gt, lt
  or or_1 (or_1_out[0], and_8_out, and_10_out);
  or or_2 (or_1_out[1], and_9_out, and_10_out);
  and and_11 (sonne, comparator_2_eq, actif_q);
  Multiplexer #(.select(2), .width(23), .enable("false")) multiplexer_2 (
    .in0({23{1'b0}}), .in1(23'h8ca0), .in2(23'h1770), .in3(23'h258), .out(multiplexer_2_out), .sel(or_1_out));
  Subtractor #(.width(23)) subtractor_2 (.a(fin_q), .b(temps), .out(subtractor_2_out));  // open: bin, bout
  Adder #(.width(23)) adder_2 (.a(multiplexer_2_out), .b(temps_prevu_q), .out(adder_2_out));  // open: cin, cout
  not not_1 (not_1_out, boutons[0]);
  Multiplexer #(.width(23), .enable("false")) multiplexer_3 (
    .in0(duree_q), .in1(subtractor_2_out), .out(multiplexer_3_out), .sel(actif_q));
  Register #(.width(23)) temps_prevu (
    .D(adder_2_out), .clk(not_1_out), .Q(temps_prevu_q), .clr(and_12_out));  // open: en
  and and_12 (and_12_out, d_ff_1_q, and_1_out);
  T_affiche t_affiche_1 (
    .regle(regle), .sous_systeme(d_ff_1_q), .temps_set(adder_2_out), .temps_restant(multiplexer_3_out),
    .clignotement(temps[2]), .Seg0(Seg0), .Seg1(Seg1), .Seg2(Seg2), .Seg3(Seg3), .Seg4(Seg4), .Seg5(Seg5));
endmodule

module T_affiche (
  input  [2:0] regle,
  input  sous_systeme,
  input  [22:0] temps_set,
  input  [22:0] temps_restant,
  input  clignotement,
  output [7:0] Seg0,
  output [7:0] Seg1,
  output [7:0] Seg2,
  output [7:0] Seg3,
  output [7:0] Seg4,
  output [7:0] Seg5
);

  wire nand_1_out, nand_2_out, nand_3_out, not_1_out;
  wire [3:0] conv_unit_dizaines_1_dizaines, conv_unit_dizaines_1_unites, conv_unit_dizaines_2_dizaines,
       conv_unit_dizaines_2_unites, conv_unit_dizaines_3_dizaines, conv_unit_dizaines_3_unites;
  wire [4:0] conv_temps_1_heures;
  wire [5:0] conv_temps_1_minutes, conv_temps_1_secondes;
  wire [7:0] chiffre_7seg_1_sortie, chiffre_7seg_2_sortie, chiffre_7seg_3_sortie, chiffre_7seg_4_sortie,
       chiffre_7seg_5_sortie, chiffre_7seg_6_sortie;
  wire [22:0] multiplexer_1_out;

  Multiplexer #(.width(23), .enable("false")) multiplexer_1 (
    .in0(temps_restant), .in1(temps_set), .out(multiplexer_1_out), .sel(sous_systeme));
  Conv_temps conv_temps_1 (
    .Temps(multiplexer_1_out), .Heures(conv_temps_1_heures), .Minutes(conv_temps_1_minutes),
    .Secondes(conv_temps_1_secondes));  // open: Jours, dixiemes
  conv_unit_dizaines conv_unit_dizaines_1 (
    .entree({conv_temps_1_heures, 1'b0}), .Dizaines(conv_unit_dizaines_1_dizaines),
    .Unites(conv_unit_dizaines_1_unites));
  conv_unit_dizaines conv_unit_dizaines_2 (
    .entree(conv_temps_1_minutes), .Dizaines(conv_unit_dizaines_2_dizaines),
    .Unites(conv_unit_dizaines_2_unites));
  conv_unit_dizaines conv_unit_dizaines_3 (
    .entree(conv_temps_1_secondes), .Dizaines(conv_unit_dizaines_3_dizaines),
    .Unites(conv_unit_dizaines_3_unites));
  not not_1 (not_1_out, sous_systeme);
  Chiffre_7seg chiffre_7seg_1 (.Entree(conv_unit_dizaines_1_dizaines), .Point(1'b0), .Sortie(chiffre_7seg_1_sortie));
  Chiffre_7seg chiffre_7seg_2 (.Entree(conv_unit_dizaines_1_unites), .Point(1'b1), .Sortie(chiffre_7seg_2_sortie));
  Chiffre_7seg chiffre_7seg_3 (.Entree(conv_unit_dizaines_2_dizaines), .Point(1'b0), .Sortie(chiffre_7seg_3_sortie));
  Chiffre_7seg chiffre_7seg_4 (.Entree(conv_unit_dizaines_2_unites), .Point(1'b1), .Sortie(chiffre_7seg_4_sortie));
  Chiffre_7seg chiffre_7seg_5 (.Entree(conv_unit_dizaines_3_dizaines), .Point(1'b0), .Sortie(chiffre_7seg_5_sortie));
  Chiffre_7seg chiffre_7seg_6 (.Entree(conv_unit_dizaines_3_unites), .Point(1'b0), .Sortie(chiffre_7seg_6_sortie));
  nand nand_1 (nand_1_out, sous_systeme, regle[0], clignotement);
  nand nand_2 (nand_2_out, sous_systeme, regle[1], clignotement);
  nand nand_3 (nand_3_out, sous_systeme, regle[2], clignotement);
  Multiplexer #(.width(8), .enable("false")) multiplexer_2 (
    .in0({8{1'b0}}), .in1(chiffre_7seg_1_sortie), .out(Seg0), .sel(nand_1_out));
  Multiplexer #(.width(8), .enable("false")) multiplexer_3 (
    .in0({8{1'b0}}), .in1(chiffre_7seg_2_sortie), .out(Seg1), .sel(nand_1_out));
  Multiplexer #(.width(8), .enable("false")) multiplexer_4 (
    .in0({8{1'b0}}), .in1(chiffre_7seg_3_sortie), .out(Seg2), .sel(nand_2_out));
  Multiplexer #(.width(8), .enable("false")) multiplexer_5 (
    .in0({8{1'b0}}), .in1(chiffre_7seg_4_sortie), .out(Seg3), .sel(nand_3_out));
  Multiplexer #(.width(8), .enable("false")) multiplexer_6 (
    .in0({8{1'b0}}), .in1(chiffre_7seg_5_sortie), .out(Seg4), .sel(not_1_out));
  Multiplexer #(.width(8), .enable("false")) multiplexer_7 (
    .in0({8{1'b0}}), .in1(chiffre_7seg_6_sortie), .out(Seg5), .sel(not_1_out));
endmodule

module Conv_temps (
  input  [22:0] Temps,
  output [2:0] Jours,
  output [4:0] Heures,
  output [5:0] Minutes,
  output [5:0] Secondes,
  output [3:0] dixiemes
);

  wire [9:4] divider_4_rem;
  wire [9:6] divider_4_out;
  wire [15:0] divider_3_rem;
  wire [15:6] divider_3_out;
  wire [19:0] divider_2_rem;
  wire [19:5] divider_2_out;
  wire [22:0] divider_1_rem;
  wire [22:3] divider_1_out;

  Divider #(.width(23)) divider_1 (
    .a(Temps), .b(23'hd2f00), .out({divider_1_out, Jours}), .rem(divider_1_rem));  // open: upper
  Divider #(.width(20)) divider_2 (
    .a(divider_1_rem[19:0]), .b(20'h8ca0), .out({divider_2_out, Heures}), .rem(divider_2_rem));  // open: upper
  Divider #(.width(16)) divider_3 (
    .a(divider_2_rem[15:0]), .b(16'h258), .out({divider_3_out, Minutes}), .rem(divider_3_rem));  // open: upper
  Divider #(.width(10)) divider_4 (
    .a(divider_3_rem[9:0]), .b(10'ha), .out({divider_4_out, Secondes}), .rem({divider_4_rem, dixiemes}));  // open: upper
endmodule

module Chiffre_7seg (
  input  [3:0] Entree,
  input  Point,
  output [7:0] Sortie
);

  Dec_b dec_b_1 (.in_1(Entree[3]), .in_2(Entree[2]), .in_3(Entree[1]), .in_4(Entree[0]), .out_5(Sortie[0]));
  Dec_a dec_a_1 (.in_1(Entree[3]), .in_2(Entree[2]), .in_3(Entree[1]), .in_4(Entree[0]), .out_5(Sortie[1]));
  Dec_f dec_f_1 (.in_1(Entree[3]), .in_2(Entree[2]), .in_3(Entree[1]), .in_4(Entree[0]), .out_5(Sortie[2]));
  Dec_g dec_g_1 (.in_1(Entree[3]), .in_2(Entree[2]), .in_3(Entree[1]), .in_4(Entree[0]), .out_5(Sortie[3]));
  Dec_c dec_c_1 (.in_1(Entree[3]), .in_2(Entree[2]), .in_3(Entree[1]), .in_4(Entree[0]), .out_5(Sortie[5]));
  Dec_d dec_d_1 (.in_1(Entree[3]), .in_2(Entree[2]), .in_3(Entree[1]), .in_4(Entree[0]), .out_5(Sortie[6]));
  Dec_e dec_e_1 (.in_1(Entree[3]), .in_2(Entree[2]), .in_3(Entree[1]), .in_4(Entree[0]), .out_5(Sortie[7]));

  assign Sortie[4] = Point;
endmodule

module Dec_a (
  input  in_1,
  input  in_2,
  input  in_3,
  input  in_4,
  output out_5
);

  wire and_1_out, and_2_out, and_3_out, and_4_out, not_1_out, not_2_out, not_3_out, not_4_out, or_1_out;

  not not_1 (not_1_out, in_1);
  not not_2 (not_2_out, in_2);
  not not_3 (not_3_out, in_3);
  not not_4 (not_4_out, in_4);
  and and_1 (and_1_out, not_1_out, not_2_out, not_3_out, in_4);
  and and_2 (and_2_out, not_1_out, in_2, not_3_out, not_4_out);
  and and_3 (and_3_out, in_1, not_2_out, in_3, in_4);
  and and_4 (and_4_out, in_1, in_2, not_3_out, in_4);
  or or_1 (or_1_out, and_1_out, and_2_out, and_3_out, and_4_out);
  not not_5 (out_5, or_1_out);
endmodule

module Dec_b (
  input  in_1,
  input  in_2,
  input  in_3,
  input  in_4,
  output out_5
);

  wire and_1_out, and_2_out, and_3_out, and_4_out, and_5_out, not_1_out, not_2_out, not_3_out, not_4_out;

  not not_1 (not_1_out, in_1);
  not not_2 (not_2_out, in_2);
  not not_3 (not_3_out, in_3);
  not not_4 (not_4_out, in_4);
  and and_1 (and_1_out, not_1_out, not_2_out);
  and and_2 (and_2_out, not_2_out, not_4_out);
  and and_3 (and_3_out, not_1_out, not_3_out, not_4_out);
  and and_4 (and_4_out, not_1_out, in_3, in_4);
  and and_5 (and_5_out, in_1, not_3_out, in_4);
  or or_1 (out_5, and_1_out, and_2_out, and_3_out, and_4_out, and_5_out);
endmodule

module Dec_c (
  input  in_1,
  input  in_2,
  input  in_3,
  input  in_4,
  output out_5
);

  wire and_1_out, and_2_out, and_3_out, not_1_out, not_2_out, not_3_out, not_4_out, or_1_out;

  not not_1 (not_1_out, in_1);
  not not_2 (not_2_out, in_2);
  not not_3 (not_3_out, in_3);
  not not_4 (not_4_out, in_4);
  and and_1 (and_1_out, in_1, in_2, not_4_out);
  and and_2 (and_2_out, in_1, in_2, in_3);
  and and_3 (and_3_out, not_1_out, not_2_out, in_3, not_4_out);
  or or_1 (or_1_out, and_1_out, and_2_out, and_3_out);
  not not_5 (out_5, or_1_out);
endmodule

module Dec_d (
  input  in_1,
  input  in_2,
  input  in_3,
  input  in_4,
  output out_5
);

  wire and_1_out, and_2_out, and_3_out, and_4_out, and_5_out, not_1_out, not_2_out, not_3_out, not_4_out;

  not not_1 (not_1_out, in_1);
  not not_2 (not_2_out, in_2);
  not not_3 (not_3_out, in_3);
  not not_4 (not_4_out, in_4);
  and and_1 (and_1_out, in_1, not_3_out);
  and and_2 (and_2_out, in_2, in_3, not_4_out);
  and and_3 (and_3_out, not_2_out, in_3, in_4);
  and and_4 (and_4_out, not_1_out, not_2_out, not_4_out);
  and and_5 (and_5_out, in_2, not_3_out, in_4);
  or or_1 (out_5, and_1_out, and_2_out, and_3_out, and_4_out, and_5_out);
endmodule

module Dec_e (
  input  in_1,
  input  in_2,
  input  in_3,
  input  in_4,
  output out_5
);

  wire and_1_out, and_2_out, and_3_out, and_4_out, not_1_out, not_2_out, not_3_out, not_4_out;

  not not_1 (not_1_out, in_1);
  not not_2 (not_2_out, in_2);
  not not_3 (not_3_out, in_3);
  not not_4 (not_4_out, in_4);
  and and_1 (and_1_out, in_1, in_2);
  and and_2 (and_2_out, in_1, in_3);
  and and_3 (and_3_out, not_2_out, not_4_out);
  and and_4 (and_4_out, in_3, not_4_out);
  or or_1 (out_5, and_1_out, and_2_out, and_3_out, and_4_out);
endmodule

module Dec_f (
  input  in_1,
  input  in_2,
  input  in_3,
  input  in_4,
  output out_5
);

  wire and_1_out, and_2_out, and_3_out, and_4_out, not_1_out, not_2_out, not_3_out, not_4_out, or_1_out;

  not not_1 (not_1_out, in_1);
  not not_2 (not_2_out, in_2);
  not not_3 (not_3_out, in_3);
  not not_4 (not_4_out, in_4);
  and and_1 (and_1_out, in_1, in_2, not_3_out, in_4);
  and and_2 (and_2_out, not_1_out, in_3, in_4);
  and and_3 (and_3_out, not_1_out, not_2_out, in_3);
  and and_4 (and_4_out, not_1_out, not_2_out, in_4);
  or or_1 (or_1_out, and_1_out, and_2_out, and_3_out, and_4_out);
  not not_5 (out_5, or_1_out);
endmodule

module Dec_g (
  input  in_1,
  input  in_2,
  input  in_3,
  input  in_4,
  output out_5
);

  wire and_1_out, and_2_out, and_3_out, not_1_out, not_2_out, not_3_out, not_4_out, or_1_out;

  not not_1 (not_1_out, in_1);
  not not_2 (not_2_out, in_2);
  not not_3 (not_3_out, in_3);
  not not_4 (not_4_out, in_4);
  and and_1 (and_1_out, not_1_out, not_2_out, not_3_out);
  and and_2 (and_2_out, in_1, in_2, not_3_out, not_4_out);
  and and_3 (and_3_out, not_1_out, in_2, in_3, in_4);
  or or_1 (or_1_out, and_1_out, and_2_out, and_3_out);
  not not_5 (out_5, or_1_out);
endmodule

module conv_unit_dizaines (
  input  [5:0] entree,
  output [3:0] Dizaines,
  output [3:0] Unites
);

  wire [5:4] divider_1_out, divider_1_rem;

  Divider #(.width(6)) divider_1 (
    .a(entree), .b(6'b001010), .out({divider_1_out, Dizaines}), .rem({divider_1_rem, Unites}));  // open: upper
endmodule
